// Logisim project CPU.circ as structural Verilog: 8 circuits, main circuit main
module main (
  input  in_1,
  output [31:0] out_2,
  output [31:0] out_3,
  output out_4,
  output [4:0] out_5,
  output [31:0] out_6,
  output out_7,
  output [31:0] out_8,
  output [31:0] out_9
);

  wire ALUB, and_1_out, Branch, clk, comparator_1_eq, counter_1_q, MemRead, MemWriteByC, RegWriteByC,
       WriteAofReg, Zero;
  wire [1:0] ExtendSel, WriteDofReg;
  wire [2:0] ALU_operation, ALUOP;
  wire [31:0] adder_1_out, adder_2_out, ALUresult, DMRD, multiplexer_7_out, NPC, PC_q, RD1, SignExt,
       subtractor_1_out;

  Multiplexer #(.width(32)) multiplexer_1 (.in0(32'h3000), .in1(PC_q), .out(out_3), .sel(counter_1_q));  // open: en
  Register #(.width(32)) PC (.D(NPC), .Q(PC_q), .clk(clk), .clr(in_1));  // open: en
  Counter #(.width(1), .max('h1), .ongoal("stay")) counter_1 (
    .Q(counter_1_q), .clk(clk), .clr(in_1));  // open: load, D, count, carry
  Adder #(.width(32)) adder_1 (.a(32'h4), .b(out_3), .out(adder_1_out));  // open: cin, cout
  Subtractor #(.width(32)) subtractor_1 (.a(out_3), .b(32'h3000), .out(subtractor_1_out));  // open: bin, bout
  Comparator #(.width(32)) comparator_1 (.a(out_2), .b({32{1'b0}}), .eq(comparator_1_eq));  // open: gt, lt
  Adder #(.width(32)) adder_2 (.a({SignExt[29:0], 2'b00}), .b(adder_1_out), .out(adder_2_out));  // open: cin, cout
  \主控单元  \u_主控单元_1  (
    .Op(out_2[31:26]), .RegWrite(RegWriteByC), .MemRead(MemRead), .MemWrite(MemWriteByC), .Branch(Branch),
    .WriteAofReg(WriteAofReg), .ALUOP(ALUOP), .WriteDtoReg(WriteDofReg), .ALUB(ALUB), .ExtendSel(ExtendSel));
  Multiplexer multiplexer_2 (.in0(RegWriteByC), .in1(1'b0), .out(out_4), .sel(comparator_1_eq));  // open: en
  Multiplexer #(.width(32)) multiplexer_3 (
    .in0(adder_1_out), .in1(adder_2_out), .out(NPC), .sel(and_1_out));  // open: en
  and and_1 (and_1_out, Zero, Branch);
  ROM #(.addrWidth(12), .dataWidth(32)) rom_1 (.addr(subtractor_1_out[13:2]), .data(out_2));  // open: sel
  Multiplexer multiplexer_4 (.in0(MemWriteByC), .in1(1'b0), .out(out_7), .sel(comparator_1_eq));  // open: en
  \ALU控制单元  \alu控制单元_1  (.Func(out_2[5:0]), .ALUOP(ALUOP), .ALU_operation(ALU_operation));
  // GRF grf_1: pin names not known; wires that end beside it: out_2[25:21], out_2[20:16], out_5, out_6, clk, in_1, out_4, RD1, out_9
  Multiplexer #(.width(5), .enable("false")) multiplexer_5 (
    .in0(out_2[20:16]), .in1(out_2[15:11]), .out(out_5), .sel(WriteAofReg));
  Multiplexer #(.select(2), .width(32)) multiplexer_6 (
    .in0(ALUresult), .in1(DMRD), .in2({out_2[15:0], {16{1'b0}}}), .out(out_6), .sel(WriteDofReg));  // open: in3, en
  // Probe on ALU_operation
  ALU alu_1 (.A(RD1), .B(multiplexer_7_out), .ALU_operation(ALU_operation), .zero(Zero), .ALU_result(ALUresult));
  EXT ext_1 (.in(out_2[15:0]), .extendSignal(ExtendSel), .out(SignExt));
  Multiplexer #(.width(32)) multiplexer_7 (
    .in0(out_9), .in1(SignExt), .out(multiplexer_7_out), .sel(ALUB));  // open: en
  DM dm_1 (.A(ALUresult[13:2]), .D(out_9), .RD(DMRD), .clk(clk), .reset(in_1), .MemWrite(out_7));
  Clock clock_1 (.out(clk));
  assign out_8 = {{18{1'b0}}, {ALUresult[13:2], 2'b00}};  // Bit_Extender bit_extender_1

  // Other names for the same wires on the sheet: Func[5:0] = out_2[5:0]; Imm[15:0] = out_2[15:0]; Instr[31:0] = out_2;
  //   rd[4:0] = out_2[15:11]; MemAdder[11:0] = ALUresult[13:2]; rt[4:0] = out_2[20:16]; rs[4:0] = out_2[25:21];
  //   OP[5:0] = out_2[31:26]; MemWrite = out_7; PC[31:0] = out_3; MemData[31:0] = out_9; RD2[31:0] = out_9;
  //   RegAdder[4:0] = out_5; RegData[31:0] = out_6; RegWrite = out_4; reset = in_1

  // Notes on the sheet:
  //   IM
  //   contents of rom_1 (hex, n*v repeats v):
  //   341c0000 341d0000 34013456 210820 8c010004 ac010004 3c027878 411822 3c051234 34040005 0 ac85ffff
  //   8c83ffff 10650001 1000000d 34670404 10e3000b 0 3c087777 3508ffff 80022 34001100 e65020 34080000
  //   34090001 340a0001 10a4020 1109fffe 1000ffff
endmodule

module ALU (
  input  [31:0] A,
  input  [31:0] B,
  input  [2:0] ALU_operation,
  output zero,
  output [31:0] ALU_result
);

  wire comparator_1_eq;
  wire [31:0] adder_1_out, and_1_out, bit_extender_1_out, or_1_out, subtractor_1_out;

  assign and_1_out = A & B;  // AND_Gate and_1, 32 bits wide
  assign or_1_out = A | B;  // OR_Gate or_1, 32 bits wide
  Adder #(.width(32)) adder_1 (.a(A), .b(B), .out(adder_1_out));  // open: cin, cout
  Subtractor #(.width(32)) subtractor_1 (.a(A), .b(B), .out(subtractor_1_out));  // open: bin, bout
  Comparator #(.width(32)) comparator_1 (.a(A), .b(B), .eq(comparator_1_eq));  // open: gt, lt
  assign bit_extender_1_out = {{31{1'b0}}, comparator_1_eq};  // Bit_Extender bit_extender_1
  Multiplexer #(.select(3), .width(32)) multiplexer_1 (
    .in0(and_1_out), .in1(or_1_out), .in2(adder_1_out), .in3(subtractor_1_out), .in4(bit_extender_1_out),
    .out(ALU_result), .sel(ALU_operation));  // open: in5, in6, in7, en
  Comparator #(.width(32)) comparator_2 (.a({32{1'b0}}), .b(ALU_result), .eq(zero));  // open: gt, lt
endmodule

module DM (
  input  clk,
  input  reset,
  input  MemWrite,
  input  [11:0] A,
  input  [31:0] D,
  output [31:0] RD
);

  RAM #(.addrWidth(12), .dataWidth(32), .bus("separate")) ram_1 (
    .addr(A), .din(D), .data(RD), .str(MemWrite), .clk(clk), .clr(reset));  // open: sel, ld
endmodule

module \寄存器  (
  input  clk,
  input  reset,
  input  WE,
  input  [4:0] A1,
  input  [4:0] A2,
  input  [4:0] A3,
  input  [31:0] WD,
  output [31:0] RD1,
  output [31:0] RD2
);

  wire [31:0] _0I, _0O, _1I, _1O, _2I, _2O, _3I, _3O, _4I, _4O, _5I, _5O, _6I, _6O, _7I, _7O, _8I, _8O, _9I,
       _9O, _10I, _10O, _11I, _11O, _12I, _12O, _13I, _13O, _14I, _14O, _15I, _15O, _16I, _16O, _17I, _17O,
       _18I, _18O, _19I, _19O, _20I, _20O, _21I, _21O, _22I, _22O, _23I, _23O, _24I, _24O, _25I, _25O, _26I,
       _26O, _27I, _27O, _28I, _28O, _29I, _29O, _30I, _30O, _31I, _31O;

  Register #(.width(32)) _0 (.D(_0I), .en(1'b0), .Q(_0O), .clk(clk), .clr(reset));
  Register #(.width(32)) register_1 (.D(_8I), .Q(_8O), .clk(clk), .clr(reset));  // open: en
  Register #(.width(32)) register_2 (.D(_16I), .Q(_16O), .clk(clk), .clr(reset));  // open: en
  Register #(.width(32)) register_3 (.D(_24I), .Q(_24O), .clk(clk), .clr(reset));  // open: en
  Register #(.width(32)) register_4 (.D(_1I), .Q(_1O), .clk(clk), .clr(reset));  // open: en
  Register #(.width(32)) register_5 (.D(_9I), .Q(_9O), .clk(clk), .clr(reset));  // open: en
  Register #(.width(32)) register_6 (.D(_17I), .Q(_17O), .clk(clk), .clr(reset));  // open: en
  Register #(.width(32)) register_7 (.D(_25I), .Q(_25O), .clk(clk), .clr(reset));  // open: en
  Register #(.width(32)) register_8 (.D(_2I), .Q(_2O), .clk(clk), .clr(reset));  // open: en
  Register #(.width(32)) register_9 (.D(_10I), .Q(_10O), .clk(clk), .clr(reset));  // open: en
  Register #(.width(32)) register_10 (.D(_18I), .Q(_18O), .clk(clk), .clr(reset));  // open: en
  Register #(.width(32)) register_11 (.D(_26I), .Q(_26O), .clk(clk), .clr(reset));  // open: en
  Multiplexer #(.select(5), .width(32)) multiplexer_1 (
    .in0(_0O), .in1(_1O), .in2(_2O), .in3(_3O), .in4(_4O), .in5(_5O), .in6(_6O), .in7(_7O), .in8(_8O),
    .in9(_9O), .in10(_10O), .in11(_11O), .in12(_12O), .in13(_13O), .in14(_14O), .in15(_15O), .in16(_16O),
    .in17(_17O), .in18(_18O), .in19(_19O), .in20(_20O), .in21(_21O), .in22(_22O), .in23(_23O), .in24(_24O),
    .in25(_25O), .in26(_26O), .in27(_27O), .in28(_28O), .in29(_29O), .in30(_30O), .in31(_31O), .out(RD1),
    .sel(A1));  // open: en
  Register #(.width(32)) register_12 (.D(_3I), .Q(_3O), .clk(clk), .clr(reset));  // open: en
  Register #(.width(32)) register_13 (.D(_11I), .Q(_11O), .clk(clk), .clr(reset));  // open: en
  Register #(.width(32)) register_14 (.D(_19I), .Q(_19O), .clk(clk), .clr(reset));  // open: en
  Register #(.width(32)) register_15 (.D(_27I), .Q(_27O), .clk(clk), .clr(reset));  // open: en
  Multiplexer #(.select(5), .width(32)) multiplexer_2 (
    .in0(_0O), .in1(_1O), .in2(_2O), .in3(_3O), .in4(_4O), .in5(_5O), .in6(_6O), .in7(_7O), .in8(_8O),
    .in9(_9O), .in10(_10O), .in11(_11O), .in12(_12O), .in13(_13O), .in14(_14O), .in15(_15O), .in16(_16O),
    .in17(_17O), .in18(_18O), .in19(_19O), .in20(_20O), .in21(_21O), .in22(_22O), .in23(_23O), .in24(_24O),
    .in25(_25O), .in26(_26O), .in27(_27O), .in28(_28O), .in29(_29O), .in30(_30O), .in31(_31O), .out(RD2),
    .sel(A2));  // open: en
  Demultiplexer #(.select(5), .width(32), .tristate("true")) demultiplexer_1 (
    .out0(_0I), .out1(_1I), .out2(_2I), .out3(_3I), .out4(_4I), .out5(_5I), .out6(_6I), .out7(_7I),
    .out8(_8I), .out9(_9I), .out10(_10I), .out11(_11I), .out12(_12I), .out13(_13I), .out14(_14I),
    .out15(_15I), .out16(_16I), .out17(_17I), .out18(_18I), .out19(_19I), .out20(_20I), .out21(_21I),
    .out22(_22I), .out23(_23I), .out24(_24I), .out25(_25I), .out26(_26I), .out27(_27I), .out28(_28I),
    .out29(_29I), .out30(_30I), .out31(_31I), .in(WD), .sel(A3), .en(WE));
  Register #(.width(32)) register_16 (.D(_28I), .Q(_28O), .clk(clk), .clr(reset));  // open: en
  Register #(.width(32)) register_17 (.D(_4I), .Q(_4O), .clk(clk), .clr(reset));  // open: en
  Register #(.width(32)) register_18 (.D(_12I), .Q(_12O), .clk(clk), .clr(reset));  // open: en
  Register #(.width(32)) register_19 (.D(_20I), .Q(_20O), .clk(clk), .clr(reset));  // open: en
  Register #(.width(32)) register_20 (.D(_5I), .Q(_5O), .clk(clk), .clr(reset));  // open: en
  Register #(.width(32)) register_21 (.D(_13I), .Q(_13O), .clk(clk), .clr(reset));  // open: en
  Register #(.width(32)) register_22 (.D(_21I), .Q(_21O), .clk(clk), .clr(reset));  // open: en
  Register #(.width(32)) register_23 (.D(_29I), .Q(_29O), .clk(clk), .clr(reset));  // open: en
  Register #(.width(32)) register_24 (.D(_6I), .Q(_6O), .clk(clk), .clr(reset));  // open: en
  Register #(.width(32)) register_25 (.D(_14I), .Q(_14O), .clk(clk), .clr(reset));  // open: en
  Register #(.width(32)) register_26 (.D(_22I), .Q(_22O), .clk(clk), .clr(reset));  // open: en
  Register #(.width(32)) register_27 (.D(_30I), .Q(_30O), .clk(clk), .clr(reset));  // open: en
  Register #(.width(32)) register_28 (.D(_7I), .Q(_7O), .clk(clk), .clr(reset));  // open: en
  Register #(.width(32)) register_29 (.D(_15I), .Q(_15O), .clk(clk), .clr(reset));  // open: en
  Register #(.width(32)) register_30 (.D(_23I), .Q(_23O), .clk(clk), .clr(reset));  // open: en
  Register #(.width(32)) register_31 (.D(_31I), .Q(_31O), .clk(clk), .clr(reset));  // open: en
endmodule

module GRF (
  input  clk,
  input  reset,
  input  WE,
  input  [4:0] RA1,
  input  [4:0] RA2,
  input  [4:0] WA,
  input  [31:0] WD,
  output [31:0] RD1,
  output [31:0] RD2
);

  \寄存器  \u_寄存器_1  (.clk(clk), .reset(reset), .WE(WE), .A1(RA1), .A2(RA2), .A3(WA), .WD(WD), .RD1(RD1), .RD2(RD2));

  // Other names for the same wires on the sheet: A1[4:0] = RA1; A2[4:0] = RA2; A3[4:0] = WA
endmodule

module \主控单元  (
  input  [5:0] Op,
  output [2:0] ALUOP,
  output RegWrite,
  output [1:0] WriteDtoReg,
  output WriteAofReg,
  output MemRead,
  output MemWrite,
  output Branch,
  output ALUB,
  output [1:0] ExtendSel
);

  wire and_5_out, not_1_out, not_2_out, not_3_out, not_4_out, not_5_out, not_6_out, or_2_out, or_4_out;
  wire [2:0] bit_extender_2_out;

  not not_1 (not_1_out, Op[5]);
  not not_2 (not_2_out, Op[4]);
  not not_3 (not_3_out, Op[3]);
  not not_4 (not_4_out, Op[2]);
  not not_5 (not_5_out, Op[1]);
  not not_6 (not_6_out, Op[0]);
  and and_1 (WriteAofReg, not_1_out, not_2_out, not_3_out, not_4_out, not_5_out, not_6_out);
  and and_2 (MemRead, Op[5], not_2_out, not_3_out, not_4_out, Op[1], Op[0]);
  and and_3 (MemWrite, Op[5], not_2_out, Op[3], not_4_out, Op[1], Op[0]);
  and and_4 (Branch, not_1_out, not_2_out, not_3_out, Op[2], not_5_out, not_6_out);
  and and_5 (and_5_out, not_1_out, not_2_out, Op[3], Op[2], not_5_out, Op[0]);
  and and_6 (WriteDtoReg[1], not_1_out, not_2_out, Op[3], Op[2], Op[1], Op[0]);
  or or_1 (RegWrite, WriteAofReg, MemRead, and_5_out, WriteDtoReg[1]);
  or or_2 (or_2_out, MemRead, MemWrite);
  or or_3 (ALUB, or_2_out, and_5_out);
  or or_4 (or_4_out, or_2_out, Branch);
  assign ExtendSel = {{1{1'b0}}, or_4_out};  // Bit_Extender bit_extender_1
  assign bit_extender_2_out = {{1{1'b0}}, {WriteAofReg, Branch}};  // Bit_Extender bit_extender_2
  Multiplexer #(.width(3)) multiplexer_1 (
    .in0(bit_extender_2_out), .in1(3'b011), .out(ALUOP), .sel(and_5_out));  // open: en

  assign WriteDtoReg[0] = MemRead;

  // Notes on the sheet:
  //   R-type
  //   lw
  //   sw
  //   beq
  //   ori
  //   lui
endmodule

module EXT (
  input  [15:0] in,
  input  [1:0] extendSignal,
  output [31:0] out
);

  wire [31:0] bit_extender_1_out, bit_extender_2_out;

  assign bit_extender_1_out = {{16{1'b0}}, in};  // Bit_Extender bit_extender_1
  assign bit_extender_2_out = {{16{in[15]}}, in};  // Bit_Extender bit_extender_2
  Multiplexer #(.select(2), .width(32)) multiplexer_1 (
    .in0(bit_extender_1_out), .in1(bit_extender_2_out), .out(out), .sel(extendSignal));  // open: in2, in3, en

  // Notes on the sheet:
  //   zero
  //   sign
endmodule

module \ALU控制单元  (
  input  [5:0] Func,
  input  [2:0] ALUOP,
  output [2:0] ALU_operation
);

  wire not_1_out, not_2_out, not_3_out, not_4_out, not_5_out, not_6_out;
  wire [1:0] add_out;
  wire [2:0] R;

  not not_1 (not_1_out, Func[4]);
  not not_2 (not_2_out, Func[5]);
  not not_3 (not_3_out, Func[3]);
  not not_4 (not_4_out, Func[2]);
  not not_5 (not_5_out, Func[0]);
  not not_6 (not_6_out, Func[1]);
  and add (add_out[0], Func[5], not_1_out, not_3_out, not_4_out, not_6_out, not_5_out);
  and sub (add_out[1], Func[5], not_1_out, not_3_out, not_4_out, Func[1], not_5_out);
  // Probe on add_out
  Multiplexer #(.select(2), .width(3)) multiplexer_1 (
    .in1(3'b010), .in2(3'b011), .out(R), .sel(add_out));  // open: in0, in3, en
  Multiplexer #(.select(3), .width(3)) multiplexer_2 (
    .in0(3'b010), .in1(3'b011), .in2(R), .in3(3'b001), .out(ALU_operation), .sel(ALUOP));  // open: in4, in5, in6, in7, en
endmodule
